# Fritzing sketch XBee_LED (saved by Fritzing 0.9.3b)
breadboards: 1

parts:
  Q1 = NPN-Transistor [package="TO92 [THT]"]
  R1 = Resistor [tolerance=±5% resistance=220 package=THT]
  U1 = XBEE-1 [package=xbee-1]
  U2 = XBEE-1 [package=xbee-1]
  Part1 = Arduino Uno (Rev3) - ICSP
  D1 = LTE-302 [package=lte-302]
  R2 = Resistor [tolerance=±5% resistance=220 package=THT]
  LED1 = smd LED [color="Red (633nm)" package="0603 [SMD]"]

nets:
  GND: Q1.E, U1.GND, U2.GND, Part1.GND, LED1.cathode
  N1: Q1.B, R2.Pin_1
  N2: Q1.C, D1.C
  VDD: R1.Pin_0, U1.VDD, U2.VDD, Part1.3V3
  N3: R1.Pin_1, D1.A
  N4: U1.DIO0, R2.Pin_0
  N5: U2.DOUT, Part1.D4
  N6: U2.DIN, Part1.D5_PWM
  N7: Part1.D10_PWM/SS, LED1.anode

notes:
  3.3Vcc (+)
  GND (-)
  2P2222 NPN Transistor
